# Fritzing sketch RovFinal (saved by Fritzing 0.9.3b)
circuit board: 8.46667cm x 5.64444cm
perfboards: 1

parts:
  Part1 = Arduino Mega 2560 (Rev3)
  S1 = H-Bridge with L298N
  S2 = H-Bridge with L298N
  S3 = H-Bridge with L298N
  M1 = DC Motor
  M2 = DC Motor
  M3 = DC Motor
  M4 = DC Motor
  M5 = DC Motor
  M6 = DC Motor
  LED1 = LED - 5mm [color="Red (633nm)" package="5 mm [THT]"]
  LED2 = LED - 5mm [color="Green (555nm)" package="5 mm [THT]"]
  Part2 = Soil Moisture Sensor  # not connected
  R2 = Resistor [tolerance=±5% resistance=220 package=THT]
  Part3 = JeePlug experimenter's board
  R3 = Resistor [tolerance=±5% resistance=220 package=THT]
  Power_plug1 = Power plug
  Part4 = JeePlug experimenter's board
  ZS-042_RTC1 = ZS-042 RTC Module
  DHT1 = DHT11 Humitidy and Temperature Sensor  # not connected
  DHT3 = DHT11 Humitidy and Temperature Sensor  # not connected
  hc-sr1 = hc-sr04
  hc-sr2 = hc-sr04
  hc-sr3 = hc-sr04
  hc-sr4 = hc-sr04
  hc-sr5 = hc-sr04
  hc-sr6 = hc-sr04
  hc-sr7 = hc-sr04
  hc-sr8 = hc-sr04
  hc-sr9 = hc-sr04
  U1 = RELAY [package=relay-jzc]  # not connected
  U2 = RELAY [package=relay-jzc]  # not connected
  GY1 = MPU-6050 Board GY-521 [form="♀ (female)" package=THT]
  U3 = RS485 [package=so08]  # not connected
  Part6 = JeePlug experimenter's board
  Part7 = JeePlug experimenter's board
  Part8 = JeePlug experimenter's board  # not connected
  J1 = double row female pin header, 4 pins [form="♀ (female)"]
  J4 = double row female pin header, 10 pins [form="♀ (female)"]
  J6 = double row female pin header, 10 pins [form="♀ (female)"]
  J7 = double row female pin header, 10 pins [form="♀ (female)"]
  J3 = male pin header, 6 pins [form="♂ (male)"]
  J8 = male pin header, 6 pins [form="♂ (male)"]
  Part9 = JeePlug experimenter's board  # not connected

nets:
  VCC: Part1.5V, Part4.B3, Part4.A3, Part4.N$42, ZS-042_RTC1.VCC, hc-sr1.VCC, hc-sr2.VCC, hc-sr3.VCC, hc-sr4.VCC, hc-sr5.VCC, hc-sr6.VCC, hc-sr7.VCC, hc-sr8.VCC, GY1.pin1, Part6.N$7, Part6.N$21, Part7.N$7, Part7.N$22
  GND: Part1.GND, LED1.cathode, LED2.cathode, Part3.N$22, Part3.N$37, Part3.N$38, Power_plug1.GND, Part4.B6, Part4.B2, Part4.A2, Part4.A6, Part4.N$9, Part4.N$23, Part4.N$24, Part4.N$27, Part4.N$63, ZS-042_RTC1.GND, hc-sr1.GND, hc-sr2.GND, hc-sr3.GND, hc-sr4.GND, hc-sr5.GND, hc-sr6.GND, hc-sr7.GND, hc-sr8.GND, hc-sr9.GND, GY1.pin2, Part6.N$39, Part6.N$45, Part7.N$39, Part7.N$46
  VIN: Part1.VIN, Power_plug1.VCC, Part4.B1, Part4.A1, Part4.N$8, Part4.N$26, Part4.N$32, Part4.N$37
  N1: Part1.D22, J8.pin1
  N2: Part1.D23, J3.pin1
  N3: Part1.D24, J8.pin2
  N4: Part1.D25, J3.pin2
  N5: Part1.D26, J8.pin3
  N6: Part1.D27, J3.pin3
  N7: Part1.D28, J8.pin4
  N8: Part1.D29, J3.pin4
  N9: Part1.D30, J8.pin5
  N10: Part1.D31, J3.pin5
  N11: Part1.D32, J8.pin6
  N12: Part1.D33, J3.pin6
  12V: S1.12V, S2.12V, S3.12V, J1.pin1, J4.pin1, J6.pin1, J7.pin1
  N13: S1.GND, J7.pin2
  N14: S1.5V, J7.pin3
  N15: S1.ENA, S1.ENA-5V
  N16: S1.IN1, J7.pin7
  N17: S1.ENB, S1.ENB-5V
  N18: S1.M1-01, M2.pin_1
  N19: S1.M1-02, M2.pin_2
  N20: S1.M2-01, M1.pin_1
  N21: S1.M2-02, M1.pin_2
  N22: S2.GND, J4.pin2
  N23: S2.5V, J4.pin3
  N24: S2.ENA, S2.ENA-5V
  N25: S2.IN1, J4.pin7
  N26: S2.ENB, S2.ENB-5V
  N27: S2.M1-01, M4.pin_1
  N28: S2.M1-02, M4.pin_2
  N29: S2.M2-01, M3.pin_1
  N30: S2.M2-02, M3.pin_2
  N31: S3.GND, J6.pin2
  N32: S3.5V, J6.pin3
  N33: S3.ENA, S3.ENA-5V
  N34: S3.IN1, J6.pin7
  N35: S3.ENB, S3.ENB-5V
  N36: S3.M1-01, M6.pin_1
  N37: S3.M1-02, M6.pin_2
  N38: S3.M2-01, M5.pin_1
  N39: S3.M2-02, M5.pin_2
  N40: LED1.anode, Part3.N$39, R3.Pin_0
  N41: LED2.anode, R2.Pin_0, Part3.N$23
  N42: R2.Pin_1, Part3.B5, Part3.N$8, Part3.N$30
  N43: Part3.N$43, Part3.N$45, Part3.N$57, R3.Pin_1
  N44: hc-sr9.VCC, Part7.N$18

custom parts:
  H-Bridge with L298N: h-bridge
  DHT11 Humitidy and Temperature Sensor: DHT11 Humidity and Temperature Sensor
  MPU-6050 Board GY-521: Acelerometro y Giroscopio MPU-6050 Board GY-521
